// Logisim project TOWFIC_SINNO_202203443(LABE_01).circ as structural Verilog: 3 circuits, main circuit main
module main (
  input  [2:0] in_1,
  input  [2:0] in_2,
  output out_3
);

  wire xnor_1_out_3, xnor_2_out_3, xnor_3_out_3;

  XNOR xnor_1 (.in_1(in_1[0]), .in_2(in_2[0]), .out_3(xnor_1_out_3));
  XNOR xnor_2 (.in_1(in_1[2]), .in_2(in_2[2]), .out_3(xnor_2_out_3));
  XNOR xnor_3 (.in_1(in_1[1]), .in_2(in_2[1]), .out_3(xnor_3_out_3));
  and and_1 (out_3, xnor_1_out_3, xnor_3_out_3, xnor_2_out_3);
endmodule

module XNOR (
  input  in_1,
  input  in_2,
  output out_3
);

  wire and_1_out, and_2_out, not_1_out, not_2_out, or_1_out;

  not not_1 (not_1_out, in_1);
  not not_2 (not_2_out, in_2);
  and and_1 (and_1_out, not_1_out, in_2);
  and and_2 (and_2_out, not_2_out, in_1);
  not not_3 (out_3, or_1_out);
  or or_1 (or_1_out, and_1_out, and_2_out);
endmodule

module AND (
  input  in_1,
  input  in_2,
  output out_3
);

  and and_1 (out_3, in_1, in_2);
endmodule
